# Fritzing sketch TimberManTxControl (saved by Fritzing 0.9.3b)
breadboards: 1
stripboards: 1

parts:
  U1 = V_REG_LD1117VXX [package=78xxl]
  C2 = Ceramic Capacitor [capacitance="100 nF" package="0805 [SMD, multilayer]"]
  C3 = Ceramic Capacitor [capacitance="100 nF" package="0805 [SMD, multilayer]"]
  IC1 = MICROCONTROLLER [package=dil28-3-simon-kit]
  XTAL1 = Crystal [frequency="16 Mhz" package=THT]
  S1 = Pushbutton [package="[THT]"]
  C4 = Capacitor [package=cap-pth-small2]
  C5 = Capacitor [package=cap-pth-small2]
  S2 = Pushbutton [package="[THT]"]
  S3 = Pushbutton [package="[THT]"]
  S4 = Pushbutton [package="[THT]"]
  S5 = Pushbutton [package="[THT]"]
  S6 = Pushbutton [package="[THT]"]
  S7 = Pushbutton [package="[THT]"]
  IC2 = MICROCONTROLLER [package=dil28-3-simon-kit]
  S8 = Pushbutton [package="[THT]"]
  S9 = Pushbutton [package="[THT]"]
  S10 = Pushbutton [package="[THT]"]
  S11 = Pushbutton [package="[THT]"]
  S12 = Pushbutton [package="[THT]"]
  S13 = Pushbutton [package="[THT]"]
  S14 = Pushbutton [package="[THT]"]
  U2 = V_REG_LD1117VXX [package=78xxl]
  XTAL2 = Crystal [frequency="16 Mhz" package=THT]
  C6 = Ceramic Capacitor [capacitance="100 nF" package="0805 [SMD, multilayer]"]
  C7 = Ceramic Capacitor [capacitance="100 nF" package="0805 [SMD, multilayer]"]
  C8 = Capacitor [package=cap-pth-small2]
  C9 = Capacitor [package=cap-pth-small2]
  S15 = Toggle Switch [package=THT]
  U3 = FS1000A - 433Mhz RF Transmitter [package=THT]
  L1 = Inductor [package="400 mil [THT]"]  # not connected
  L2 = Inductor [package="400 mil [THT]"]  # not connected
  VCC1 = Battery block 9V
  R1 = Resistor [tolerance=±5% resistance=1k package=THT]

nets:
  N1: U1.OUT, C2.0, C3.1, IC1.GND, IC1.AGND, S1.Pin_3, S1.Pin_4, C4.2, C5.1
  N2: U1.GND, C5.2
  N3: U1.IN, IC1.VCC, IC1.AVCC, C4.1
  N4: C2.1, IC1.PB6(XTAL1_TOSC1), XTAL1.pin_0
  N5: C3.0, IC1.PB7(XTAL2_TOSC2), XTAL1.pin_1
  N6: IC1.PC6(_RESET), S1.Pin_1, S1.Pin_2
  N7: S2.Pin_1, S2.Pin_2
  N8: S2.Pin_3, S2.Pin_4
  N9: S3.Pin_1, S3.Pin_2
  N10: S4.Pin_1, S4.Pin_2
  N11: S4.Pin_3, S4.Pin_4
  N12: S5.Pin_1, S5.Pin_2
  N13: S5.Pin_3, S5.Pin_4
  N14: S6.Pin_1, S6.Pin_2
  N15: S6.Pin_3, S6.Pin_4
  N16: S7.Pin_1, S7.Pin_2
  N17: S7.Pin_3, S7.Pin_4
  N18: IC2.PC6(_RESET), IC2.PC5(ADC5_SCL), R1.Pin_0
  N19: IC2.PD0(RXD), IC2.PC4(ADC4_SDA)
  N20: IC2.PD1(TXD), IC2.PC3(ADC3)
  N21: IC2.PD2(INT0), IC2.PC2(ADC2), S12.Pin_3, S12.Pin_4
  N22: IC2.PD3(INT1), IC2.VCC, IC2.AGND, IC2.PC1(ADC1), S15.COM, R1.Pin_1
  N23: IC2.PD4(XCK_T0), IC2.PC0(ADC0), S12.Pin_1, S12.Pin_2, S15.L1
  N24: IC2.GND, IC2.AREF, S15.L2
  N25: IC2.PB6(XTAL1_TOSC1), IC2.AVCC, XTAL2.pin_0, C7.0, C7.1
  N26: IC2.PB7(XTAL2_TOSC2), IC2.PB5(SCK), XTAL2.pin_1, C6.0, C6.1
  N27: IC2.PD5(T1), IC2.PB4(MISO)
  N28: IC2.PD6(AIN0), IC2.PB3(MOSI_OC2), S13.Pin_3, S13.Pin_4
  N29: IC2.PD7(AIN1), IC2.PB2(SS_OC1B)
  N30: IC2.PB0(ICP), IC2.PB1(OC1A), S13.Pin_1, S13.Pin_2
  N31: S8.Pin_1, S8.Pin_2, C9.1, VCC1.-
  N32: S8.Pin_3, S8.Pin_4, U2.GND, C9.2, VCC1.+
  N33: S9.Pin_1, S9.Pin_2, S11.Pin_1, S11.Pin_2, C8.2
  N34: S9.Pin_3, S9.Pin_4, S11.Pin_3, S11.Pin_4, U2.IN, C8.1
  N35: S10.Pin_1, S10.Pin_2
  N36: S10.Pin_3, S10.Pin_4
  N37: S14.Pin_1, S14.Pin_2, U3.GND
  N38: S14.Pin_3, S14.Pin_4, U3.DATA

custom parts:
  FS1000A - 433Mhz RF Transmitter: This is 433Mhz RF transmitter with receiver kit for Arduino ARM MCU wireless Application environment: Remote control switch, receiver module, motorcycles, automobile anti-theft products, home security products, electric doors, shutter doors, windows, remote control socket, remote control LED, remote audio remote control electric doors, garage door remote control, remote control retractable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
